// Digital circuit 02And.dig as structural Verilog
module _02And (
  input  a,
  input  b,
  output out
);

  wire nand_1_out;

  nand nand_1 (nand_1_out, a, b);
  not not_1 (out, nand_1_out);
endmodule
