// Digital circuit 05Mux.dig as structural Verilog
module _05Mux (
  input  sel,
  input  b,
  input  a,
  output out
);

  wire and_1_out, and_2_out, not_1_out;

  not not_1 (not_1_out, sel);
  and and_1 (and_1_out, b, sel);
  and and_2 (and_2_out, a, not_1_out);
  or or_1 (out, and_1_out, and_2_out);
endmodule
