// Digital circuit DMux4Way.dig as structural Verilog
module DMux4Way (
  input  in,
  input  [1:0] sel,
  output a,
  output b,
  output c,
  output d
);

  wire dmux_1_a, dmux_1_b;

  DMux dmux_1 (.in(in), .sel(sel[1]), .a(dmux_1_a), .b(dmux_1_b));
  DMux dmux_2 (.in(dmux_1_a), .sel(sel[0]), .a(a), .b(b));
  DMux dmux_3 (.in(dmux_1_b), .sel(sel[0]), .a(c), .b(d));
endmodule
